# Fritzing sketch ServoTester (saved by Fritzing 0.9.3b)
breadboards: 1

parts:
  Componente1 = Arduino Uno (Rev3)
  U1 = POT [package=alps_pot]
  LED1 = LEDs [package=led10mm]
  R1 = Resistor [tolerance=±5% resistance=220 package="0805 [SMD]"]

nets:
  N1: Componente1.A0, U1.S
  N2: Componente1.D5_PWM, R1.Pin_0
  N3: Componente1.5V, U1.E
  N4: Componente1.GND, U1.A, LED1.A
  N5: LED1.C, R1.Pin_1

notes:
  Conectar al ESC.
